# Fritzing sketch mephisto_vi (saved by Fritzing 0.9.3b)
breadboards: 1

parts:
  Bauteil1 = Arduino Uno (Rev3)
  S1 = Pushbutton [package=THT]
  R1 = Resistor [tolerance=±5% resistance=220 package=THT]
  R2 = Resistor [tolerance=±5% resistance=220 package=THT]
  S2 = Pushbutton [package=THT]
  S3 = Pushbutton [package=THT]
  R3 = Resistor [tolerance=±5% resistance=220 package=THT]
  S4 = Toggle Switch [package=THT]
  S5 = Toggle Switch [package=THT]
  S6 = Toggle Switch [package=THT]
  R4 = Resistor [tolerance=±5% resistance=220 package=THT]
  R5 = Resistor [tolerance=±5% resistance=220 package=THT]
  R6 = Resistor [tolerance=±5% resistance=220 package=THT]
  RE1 = Rotary Encoder [package=THT]
  S7 = Pushbutton [package=THT]
  R7 = Resistor [tolerance=±5% resistance=220 package=THT]
  U1 = 74HC595 [package="DIP16 [THT]"]
  S8 = Pushbutton [package=THT]
  R9 = Resistor [tolerance=±5% resistance=220 package=THT]
  LED1 = LED - 5mm [color="Red (633nm)" package="5 mm [THT]"]
  R10 = Resistor [tolerance=±5% resistance=220 package=THT]

nets:
  N1: Bauteil1.A0, S6.L2, R6.Pin_0
  N2: Bauteil1.A1, S5.L2, R5.Pin_0
  N3: Bauteil1.A2, S4.L2, R4.Pin_0
  N4: Bauteil1.A3, S1.leg0, R1.Pin_0
  N5: Bauteil1.A4/SDA, R2.Pin_0, S2.leg0
  N6: Bauteil1.A5/SCL, S3.leg0, R3.Pin_0
  N7: Bauteil1.D8, U1.DS
  N8: Bauteil1.D9_PWM, U1.ST_CP
  N9: Bauteil1.D10_PWM/SS, U1.SH_CP
  N10: Bauteil1.D2, RE1.EncoderPinA
  N11: Bauteil1.D3_PWM, RE1.EncoderPinB
  N12: Bauteil1.D4, S8.leg0, R9.Pin_0
  N13: Bauteil1.D7, S7.leg0, R7.Pin_0
  3V3: Bauteil1.3V3, R1.Pin_1, R2.Pin_1, R3.Pin_1, R4.Pin_1, R5.Pin_1, R6.Pin_1, R7.Pin_1, U1.MR, U1.VCC, R9.Pin_1
  N14: S1.leg1, S2.leg1, S3.leg1, RE1.EncoderPinC, U1.GND, U1.OE
  N15: S4.COM, S5.COM, S6.COM, S7.leg1, S8.leg1, LED1.anode
  N16: U1.Q1, LED1.cathode, R10.Pin_0, R10.Pin_1
